# Fritzing sketch hitachi_display_i2c (saved by Fritzing 0.7.11b)
stripboards: 1

parts:
  U2 = atmega168 [package=dip]
  Y1 = Resonator [frequency="16 Mhz" package=THT]
  J2 = male pin header, 7 pins [form="♂ (male)"]
  LCD1 = LCD screen
  R1 = Trimmer Potentiometer [maximum_resistance=10kΩ package=THT]

nets:
  N1: U2.D0_(RX), J2.pin1, J2.pin6
  N2: U2.D1_(TX), J2.pin7
  N3: U2.D2, LCD1.DB7
  N4: U2.D3_(PWM), LCD1.DB6
  N5: U2.D4, LCD1.DB5
  VCC: U2.VCC, LCD1.VDD, LCD1.DB1, LCD1.LED+, R1.leg1
  GND: U2.GND#7, Y1.GND, LCD1.VSS, LCD1.R/W, LCD1.DB3, LCD1.LED-, R1.leg2
  N6: U2.XLAT1, Y1.pin_1
  N7: U2.XLAT2, Y1.0
  N8: U2.D5_(PWM), LCD1.DB4
  N9: U2.D11_(PWM), LCD1.E
  N10: U2.D12, LCD1.RS
  N11: U2.AVCC, J2.pin5
  N12: U2.GND#21, J2.pin4
  N13: U2.A4, J2.pin2
  N14: U2.A5, J2.pin3
  N15: LCD1.V0, LCD1.DB2, R1.wiper
